// Logisim project TallerLogica-Combinatorios.circ as structural Verilog: 9 circuits, main circuit sumador_simple
module sumador_simple (
  input  A,
  input  B,
  output S,
  output Cout
);

  and and_1 (Cout, A, B);
  xor xor_1 (S, A, B);
endmodule

module sumador_completo (
  input  Cin,
  input  A,
  input  B,
  output S,
  output Cout
);

  wire sumador_simple_1_cout, sumador_simple_1_s, sumador_simple_2_cout;

  sumador_simple sumador_simple_1 (.A(A), .B(B), .S(sumador_simple_1_s), .Cout(sumador_simple_1_cout));
  sumador_simple sumador_simple_2 (.A(Cin), .B(sumador_simple_1_s), .S(S), .Cout(sumador_simple_2_cout));
  or or_1 (Cout, sumador_simple_2_cout, sumador_simple_1_cout);
endmodule

module sumador_4 (
  input  Cin,
  input  [3:0] A,
  input  [3:0] B,
  output [3:0] S,
  output Cout
);

  wire sumador_completo_1_cout, sumador_completo_2_cout, sumador_completo_3_cout;

  sumador_completo sumador_completo_1 (.Cin(Cin), .A(A[0]), .B(B[0]), .S(S[0]), .Cout(sumador_completo_1_cout));
  sumador_completo sumador_completo_2 (
    .Cin(sumador_completo_1_cout), .A(A[1]), .B(B[1]), .S(S[1]), .Cout(sumador_completo_2_cout));
  sumador_completo sumador_completo_3 (
    .Cin(sumador_completo_2_cout), .A(A[2]), .B(B[2]), .S(S[2]), .Cout(sumador_completo_3_cout));
  sumador_completo sumador_completo_4 (.Cin(sumador_completo_3_cout), .A(A[3]), .B(B[3]), .S(S[3]), .Cout(Cout));
  Hex_Digit_Display hex_digit_display_1 (.value(S));  // open: dp
endmodule

module comparador_cero (
  input  [3:0] A,
  output Z
);

  wire or_1_out, or_2_out, or_3_out;

  or or_1 (or_1_out, A[0], A[1]);
  or or_2 (or_2_out, A[2], A[3]);
  or or_3 (or_3_out, or_1_out, or_2_out);
  not not_1 (Z, or_3_out);
endmodule

module sumador_flags (
  input  Cin,
  input  [3:0] A,
  input  [3:0] B,
  output [3:0] S,
  output C,
  output Z,
  output N,
  output V
);

  wire not_1_out, xor_1_out, xor_2_out;

  sumador_4 sumador_4_1 (.Cin(Cin), .A(A), .B(B), .S({N, S[2:0]}), .Cout(C));
  xor xor_1 (xor_1_out, A[3], B[3]);
  not not_1 (not_1_out, xor_1_out);
  xor xor_2 (xor_2_out, B[3], N);
  and and_1 (V, not_1_out, xor_2_out);
  Hex_Digit_Display hex_digit_display_1 (.value({N, S[2:0]}));  // open: dp
  comparador_cero comparador_cero_1 (.A({N, S[2:0]}), .Z(Z));

  assign S[3] = N;
endmodule

module incrementador_4 (
  input  [3:0] A,
  output [3:0] S
);

  sumador_4 sumador_4_1 (.Cin(1'b0), .A(4'b0001), .B(A), .S(S));  // open: Cout
  Hex_Digit_Display hex_digit_display_1 (.value(S));  // open: dp
endmodule

module inversor_4 (
  input  [3:0] A,
  input  INV,
  output [3:0] S
);

  xor xor_1 (S[0], A[0], INV);
  xor xor_2 (S[1], A[1], INV);
  xor xor_3 (S[2], A[2], INV);
  xor xor_4 (S[3], A[3], INV);
  Hex_Digit_Display hex_digit_display_1 (.value(S));  // open: dp
endmodule

module ALU (
  input  [3:0] A,
  input  [3:0] B,
  input  [1:0] OP,
  output N,
  output Z,
  output V,
  output C,
  output [3:0] S
);

  Hex_Digit_Display hex_digit_display_1 (.value(S));  // open: dp
endmodule

module verificador (
  output [3:0] out_1,
  output [3:0] out_2,
  output [1:0] out_3,
  output halt,
  output N,
  output Z,
  output V,
  output C,
  output [3:0] res
);

  wire clock_1_out;

  Clock clock_1 (.out(clock_1_out));
  Counter #(.max('h3ff), .width(10)) counter_1 (
    .clk(clock_1_out), .carry(halt), .Q({out_3, out_2, out_1}));  // open: clr, load, up, count, D
  ALU alu_1 (.A(out_1), .B(out_2), .OP(out_3), .N(N), .Z(Z), .V(V), .C(C), .S(res));
endmodule
